# Fritzing sketch pill_E (saved by Fritzing 0.9.4)
breadboards: 1

parts:
  WeMos_D1_Mini1 = WeMos D1 Mini
  S3 = Pushbutton [package="[SMD]"]
  R2 = Resistor [tolerance=±5% resistance=10k package="1206 [SMD]"]
  U1 = LIPO-110mAh [package=lipo-110]

nets:
  N1: WeMos_D1_Mini1.5V, S3.Pin_3, S3.Pin_4, U1.+
  N2: WeMos_D1_Mini1.D2, S3.Pin_1, S3.Pin_2, R2.Pin_1, U1.-
  N3: WeMos_D1_Mini1.G, R2.Pin_0
